// Logisim project ALU.circ as structural Verilog: 4 circuits, main circuit 1-bit adder
module ALU (
  input  in_1,
  input  in_2,
  input  in_3,
  input  in_4,
  input  [1:0] in_5,
  input  in_6,
  input  [1:0] in_7,
  input  in_8,
  input  [1:0] in_9,
  input  in_10,
  input  in_11,
  input  in_12,
  input  in_13,
  input  [1:0] in_14,
  input  in_15,
  input  in_16,
  input  in_17,
  output Overflow,
  output Overflow_2
);

  wire and_1_out, and_2_out, and_3_out, and_4_out, clock_1_out, demultiplexer_1_out0, demultiplexer_1_out1,
       demultiplexer_1_out2, demultiplexer_1_out3, multiplexer_5_out, multiplexer_6_out, multiplexer_7_out,
       multiplexer_8_out, multiplexer_9_out, multiplexer_10_out, multiplexer_11_out, multiplexer_12_out,
       or_1_out, or_2_out, or_3_out, or_4_out, register_1_q, register_2_q, register_3_q, register_4_q,
       register_5_q, register_6_q, register_7_q, register_8_q, register_9_q, register_10_q, register_11_q,
       register_12_q, register_13_q, register_14_q, register_15_q, register_16_q, xor_1_out, xor_2_out,
       xor_3_out, xor_4_out;

  Register #(.width(1)) register_1 (.D(in_1), .Q(register_1_q), .clk(demultiplexer_1_out0));  // open: en, clr
  Register #(.width(1)) register_2 (.D(in_2), .Q(register_2_q), .clk(demultiplexer_1_out0));  // open: en, clr
  Register #(.width(1)) register_3 (.D(in_3), .Q(register_3_q), .clk(demultiplexer_1_out0));  // open: en, clr
  Register #(.width(1)) register_4 (.D(in_4), .Q(register_4_q), .clk(demultiplexer_1_out0));  // open: en, clr
  Multiplexer #(.select(2)) multiplexer_1 (
    .in0(register_1_q), .in1(register_5_q), .in2(register_9_q), .in3(register_13_q), .out(in_1), .sel(in_9),
    .en(in_10));
  LED led_1 (.in(in_1));
  Register #(.width(1)) register_5 (.D(in_1), .Q(register_5_q), .clk(demultiplexer_1_out1));  // open: en, clr
  Register #(.width(1)) register_6 (.D(in_2), .Q(register_6_q), .clk(demultiplexer_1_out1));  // open: en, clr
  Register #(.width(1)) register_7 (.D(in_3), .Q(register_7_q), .clk(demultiplexer_1_out1));  // open: en, clr
  Register #(.width(1)) register_8 (.D(in_4), .Q(register_8_q), .clk(demultiplexer_1_out1));  // open: en, clr
  Register #(.width(1)) register_9 (.D(in_1), .Q(register_9_q), .clk(demultiplexer_1_out2));  // open: en, clr
  Register #(.width(1)) register_10 (.D(in_2), .Q(register_10_q), .clk(demultiplexer_1_out2));  // open: en, clr
  Register #(.width(1)) register_11 (.D(in_3), .Q(register_11_q), .clk(demultiplexer_1_out2));  // open: en, clr
  Register #(.width(1)) register_12 (.D(in_4), .Q(register_12_q), .clk(demultiplexer_1_out2));  // open: en, clr
  Multiplexer #(.select(2)) multiplexer_2 (
    .in0(register_2_q), .in1(register_6_q), .in2(register_10_q), .in3(register_14_q), .out(in_2), .sel(in_9),
    .en(in_10));
  LED led_2 (.in(in_2));
  Register #(.width(1)) register_13 (.D(in_1), .Q(register_13_q), .clk(demultiplexer_1_out3));  // open: en, clr
  Register #(.width(1)) register_14 (.D(in_2), .Q(register_14_q), .clk(demultiplexer_1_out3));  // open: en, clr
  Register #(.width(1)) register_15 (.D(in_3), .Q(register_15_q), .clk(demultiplexer_1_out3));  // open: en, clr
  Register #(.width(1)) register_16 (.D(in_4), .Q(register_16_q), .clk(demultiplexer_1_out3));  // open: en, clr
  Multiplexer #(.select(2)) multiplexer_3 (
    .in0(register_3_q), .in1(register_7_q), .in2(register_11_q), .in3(register_15_q), .out(in_3), .sel(in_9),
    .en(in_10));
  LED led_3 (.in(in_3));
  Multiplexer #(.select(2)) multiplexer_4 (
    .in0(register_4_q), .in1(register_8_q), .in2(register_12_q), .in3(register_16_q), .out(in_4), .sel(in_9),
    .en(in_10));
  LED led_4 (.in(in_4));
  Demultiplexer #(.select(2)) demultiplexer_1 (
    .out0(demultiplexer_1_out0), .out1(demultiplexer_1_out1), .out2(demultiplexer_1_out2),
    .out3(demultiplexer_1_out3), .in(clock_1_out), .sel(in_5), .en(in_6));
  Clock clock_1 (.out(clock_1_out));
  LED led_5 (.in(multiplexer_5_out));
  Multiplexer #(.select(2)) multiplexer_5 (
    .in0(register_1_q), .in1(register_5_q), .in2(register_9_q), .in3(register_13_q), .out(multiplexer_5_out),
    .sel(in_7), .en(in_15));
  Multiplexer #(.select(2)) multiplexer_6 (
    .in0(register_2_q), .in1(register_6_q), .in2(register_10_q), .in3(register_14_q),
    .out(multiplexer_6_out), .sel(in_7), .en(in_15));
  Multiplexer #(.select(2)) multiplexer_7 (
    .in0(register_3_q), .in1(register_7_q), .in2(register_11_q), .in3(register_15_q),
    .out(multiplexer_7_out), .sel(in_7), .en(in_15));
  Multiplexer #(.select(2)) multiplexer_8 (
    .in0(register_4_q), .in1(register_8_q), .in2(register_12_q), .in3(register_16_q),
    .out(multiplexer_8_out), .sel(in_7), .en(in_15));
  LED led_6 (.in(multiplexer_8_out));
  LED led_7 (.in(multiplexer_9_out));
  Multiplexer #(.select(2)) multiplexer_9 (
    .in0(register_1_q), .in1(register_5_q), .in2(register_9_q), .in3(register_13_q), .out(multiplexer_9_out),
    .sel(in_14), .en(in_15));
  Multiplexer #(.select(2)) multiplexer_10 (
    .in0(register_2_q), .in1(register_6_q), .in2(register_10_q), .in3(register_14_q),
    .out(multiplexer_10_out), .sel(in_14), .en(in_15));
  LED led_8 (.in(multiplexer_10_out));
  LED led_9 (.in(multiplexer_11_out));
  Multiplexer #(.select(2)) multiplexer_11 (
    .in0(register_3_q), .in1(register_7_q), .in2(register_11_q), .in3(register_15_q),
    .out(multiplexer_11_out), .sel(in_14), .en(in_15));
  Multiplexer #(.select(2)) multiplexer_12 (
    .in0(register_4_q), .in1(register_8_q), .in2(register_12_q), .in3(register_16_q),
    .out(multiplexer_12_out), .sel(in_14), .en(in_15));
  LED led_10 (.in(multiplexer_12_out));
  LED led_11 (.in(multiplexer_6_out));
  LED led_12 (.in(multiplexer_7_out));
  assign in_1 = in_8 ? and_1_out : 1'bz;  // Controlled_Buffer controlled_buffer_1
  and and_1 (and_1_out, multiplexer_5_out, multiplexer_9_out);
  and and_2 (and_2_out, multiplexer_6_out, multiplexer_10_out);
  assign in_2 = in_8 ? and_2_out : 1'bz;  // Controlled_Buffer controlled_buffer_2
  assign in_3 = in_8 ? and_3_out : 1'bz;  // Controlled_Buffer controlled_buffer_3
  and and_3 (and_3_out, multiplexer_7_out, multiplexer_11_out);
  and and_4 (and_4_out, multiplexer_8_out, multiplexer_12_out);
  assign in_4 = in_8 ? and_4_out : 1'bz;  // Controlled_Buffer controlled_buffer_4
  or or_1 (or_1_out, multiplexer_5_out, multiplexer_9_out);
  assign in_1 = in_11 ? or_1_out : 1'bz;  // Controlled_Buffer controlled_buffer_5
  assign in_2 = in_11 ? or_2_out : 1'bz;  // Controlled_Buffer controlled_buffer_6
  or or_2 (or_2_out, multiplexer_6_out, multiplexer_10_out);
  or or_3 (or_3_out, multiplexer_7_out, multiplexer_11_out);
  assign in_3 = in_11 ? or_3_out : 1'bz;  // Controlled_Buffer controlled_buffer_7
  assign in_4 = in_11 ? or_4_out : 1'bz;  // Controlled_Buffer controlled_buffer_8
  or or_4 (or_4_out, multiplexer_8_out, multiplexer_12_out);
  xor xor_1 (xor_1_out, multiplexer_5_out, multiplexer_9_out);
  assign in_1 = in_12 ? xor_1_out : 1'bz;  // Controlled_Buffer controlled_buffer_9
  assign in_2 = in_12 ? xor_2_out : 1'bz;  // Controlled_Buffer controlled_buffer_10
  xor xor_2 (xor_2_out, multiplexer_6_out, multiplexer_10_out);
  xor xor_3 (xor_3_out, multiplexer_7_out, multiplexer_11_out);
  assign in_3 = in_12 ? xor_3_out : 1'bz;  // Controlled_Buffer controlled_buffer_11
  xor xor_4 (xor_4_out, multiplexer_8_out, multiplexer_12_out);
  assign in_1 = in_13 ? ~multiplexer_5_out : 1'bz;  // Controlled_Inverter controlled_inverter_1
  assign in_2 = in_13 ? ~multiplexer_6_out : 1'bz;  // Controlled_Inverter controlled_inverter_2
  assign in_3 = in_13 ? ~multiplexer_7_out : 1'bz;  // Controlled_Inverter controlled_inverter_3
  _4_bit_adder u_4_bit_adder_1 (
    .A0(multiplexer_5_out), .A1(multiplexer_6_out), .A2(multiplexer_7_out), .A3(multiplexer_8_out),
    .B0(multiplexer_9_out), .B1(multiplexer_10_out), .B2(multiplexer_11_out), .B3(multiplexer_12_out),
    .in_1(in_16), .Overflow(Overflow), .out_10(in_1), .out_11(in_2), .out_12(in_3), .out_13(in_4));
  Substractor substractor_1 (
    .A0(multiplexer_5_out), .A1(multiplexer_6_out), .A2(multiplexer_7_out), .A3(multiplexer_8_out),
    .B0(multiplexer_9_out), .B1(multiplexer_10_out), .B2(multiplexer_11_out), .B3(multiplexer_12_out),
    .in_2(in_17), .Overflow(Overflow_2), .out_10(in_1), .out_11(in_2), .out_12(in_3), .out_13(in_4));
  LED led_13 (.in(in_4));
  assign in_4 = in_12 ? xor_4_out : 1'bz;  // Controlled_Buffer controlled_buffer_12
  assign in_4 = in_13 ? ~multiplexer_8_out : 1'bz;  // Controlled_Inverter controlled_inverter_4

  // Notes on the sheet:
  //   Registro 00
  //   Registro 01
  //   Registro 10
  //   Registro 11
  //   Indice de entrada
  //   Reloj
endmodule

module _1_bit_adder (
  input  C_in,
  input  A,
  input  B,
  output Sum,
  output C_out
);

  wire and_1_out, and_2_out, and_3_out, xor_2_out;

  and and_1 (and_1_out, C_in, A);
  and and_2 (and_2_out, C_in, B);
  and and_3 (and_3_out, A, B);
  xor xor_1 (Sum, C_in, xor_2_out);
  xor xor_2 (xor_2_out, A, B);
  or or_1 (C_out, and_1_out, and_2_out, and_3_out);
endmodule

module _4_bit_adder (
  input  in_1,
  input  A0,
  input  A1,
  input  A2,
  input  A3,
  input  B0,
  input  B1,
  input  B2,
  input  B3,
  output out_10,
  output out_11,
  output out_12,
  output out_13,
  output Overflow
);

  wire n1_bit_adder_1_c_out, n1_bit_adder_2_c_out, n1_bit_adder_3_c_out;

  _1_bit_adder u_1_bit_adder_1 (.A(A0), .B(B0), .C_in(in_1), .C_out(n1_bit_adder_1_c_out), .Sum(out_10));
  _1_bit_adder u_1_bit_adder_2 (
    .A(A1), .B(B1), .C_in(n1_bit_adder_1_c_out), .C_out(n1_bit_adder_2_c_out), .Sum(out_11));
  _1_bit_adder u_1_bit_adder_3 (
    .A(A2), .B(B2), .C_in(n1_bit_adder_2_c_out), .C_out(n1_bit_adder_3_c_out), .Sum(out_12));
  _1_bit_adder u_1_bit_adder_4 (.A(A3), .B(B3), .C_in(n1_bit_adder_3_c_out), .C_out(Overflow), .Sum(out_13));
endmodule

module Substractor (
  input  A0,
  input  in_2,
  input  A1,
  input  A2,
  input  A3,
  input  B0,
  input  B1,
  input  B2,
  input  B3,
  output out_10,
  output out_11,
  output out_12,
  output out_13,
  output Overflow
);

  wire n1_bit_adder_1_c_out, n1_bit_adder_2_c_out, n1_bit_adder_3_c_out, not_1_out, not_2_out, not_3_out,
       not_4_out;

  not not_1 (not_1_out, B2);
  not not_2 (not_2_out, B1);
  not not_3 (not_3_out, B0);
  not not_4 (not_4_out, B3);
  _1_bit_adder u_1_bit_adder_1 (.A(A0), .B(not_3_out), .C_in(in_2), .C_out(n1_bit_adder_1_c_out), .Sum(out_10));
  _1_bit_adder u_1_bit_adder_2 (
    .A(A1), .B(not_2_out), .C_in(n1_bit_adder_1_c_out), .C_out(n1_bit_adder_2_c_out), .Sum(out_11));
  _1_bit_adder u_1_bit_adder_3 (
    .A(A2), .B(not_1_out), .C_in(n1_bit_adder_2_c_out), .C_out(n1_bit_adder_3_c_out), .Sum(out_12));
  _1_bit_adder u_1_bit_adder_4 (.A(A3), .B(not_4_out), .C_in(n1_bit_adder_3_c_out), .C_out(Overflow), .Sum(out_13));
endmodule
