// Logisim project Adder.circ as structural Verilog: 2 circuits, main circuit 1-bit adder
module _1_bit_adder (
  input  C_in,
  input  A,
  input  B,
  output Sum,
  output C_out
);

  wire and_1_out, and_2_out, and_3_out, xor_2_out;

  and and_1 (and_1_out, C_in, A);
  and and_2 (and_2_out, C_in, B);
  and and_3 (and_3_out, A, B);
  xor xor_1 (Sum, C_in, xor_2_out);
  xor xor_2 (xor_2_out, A, B);
  or or_1 (C_out, and_1_out, and_2_out, and_3_out);
endmodule

module _4_bit_adder (
  input  in_1,
  input  [3:0] A,
  input  [3:0] B,
  output out_4,
  output out_5,
  output out_6,
  output out_7,
  output Overflow
);

  wire n1_bit_adder_1_c_out, n1_bit_adder_2_c_out, n1_bit_adder_3_c_out;

  _1_bit_adder u_1_bit_adder_1 (.A(A[0]), .B(B[0]), .C_in(in_1), .C_out(n1_bit_adder_1_c_out), .Sum(out_4));
  _1_bit_adder u_1_bit_adder_2 (
    .A(A[1]), .B(B[1]), .C_in(n1_bit_adder_1_c_out), .C_out(n1_bit_adder_2_c_out), .Sum(out_5));
  _1_bit_adder u_1_bit_adder_3 (
    .A(A[2]), .B(B[2]), .C_in(n1_bit_adder_2_c_out), .C_out(n1_bit_adder_3_c_out), .Sum(out_6));
  _1_bit_adder u_1_bit_adder_4 (.A(A[3]), .B(B[3]), .C_in(n1_bit_adder_3_c_out), .C_out(Overflow), .Sum(out_7));
endmodule
