// Logisim project Substractor.circ as structural Verilog: 2 circuits, main circuit Adder
module Adder (
  input  C_in,
  input  A,
  input  B,
  output Sum,
  output C_out
);

  wire and_1_out, and_2_out, and_3_out, xor_2_out;

  and and_1 (and_1_out, C_in, A);
  and and_2 (and_2_out, C_in, B);
  and and_3 (and_3_out, A, B);
  xor xor_1 (Sum, C_in, xor_2_out);
  xor xor_2 (xor_2_out, A, B);
  or or_1 (C_out, and_1_out, and_2_out, and_3_out);
endmodule

module Substractor (
  input  in_1,
  input  [3:0] A,
  input  [3:0] B,
  output out_4,
  output out_5,
  output out_6,
  output out_7,
  output Overflow
);

  wire adder_1_c_out, adder_2_c_out, adder_3_c_out, not_1_out, not_2_out, not_3_out, not_4_out;

  not not_1 (not_1_out, B[2]);
  not not_2 (not_2_out, B[0]);
  not not_3 (not_3_out, B[1]);
  not not_4 (not_4_out, B[3]);
  Adder adder_1 (.A(A[0]), .B(not_2_out), .C_in(in_1), .C_out(adder_1_c_out), .Sum(out_4));
  Adder adder_2 (.A(A[1]), .B(not_3_out), .C_in(adder_1_c_out), .C_out(adder_2_c_out), .Sum(out_5));
  Adder adder_3 (.A(A[2]), .B(not_1_out), .C_in(adder_2_c_out), .C_out(adder_3_c_out), .Sum(out_6));
  Adder adder_4 (.A(A[3]), .B(not_4_out), .C_in(adder_3_c_out), .C_out(Overflow), .Sum(out_7));
endmodule
